// Logisim project logisim.circ as structural Verilog: 6 circuits, main circuit main
module main (
  input  [3:0] A,
  input  [3:0] B,
  input  [3:0] in_3,
  input  [1:0] in_4,
  output out_5
);

  wire [3:0] aand_1_out_3, oor_1_out_3, ssomador4_1_s, xxor_1_out_3;

  AAND aand_1 (.A(A), .B(B), .out_3(aand_1_out_3));
  OOR oor_1 (.A(A), .B(B), .out_3(oor_1_out_3));
  XXOR xxor_1 (.A(A), .B(B), .out_3(xxor_1_out_3));
  SSOMADOR4 ssomador4_1 (.A(A), .B(B), .S(ssomador4_1_s), .Carry(out_5));
  // Probe on oor_1_out_3
  // Probe on xxor_1_out_3
  // Probe on aand_1_out_3
  Multiplexer #(.select(2), .width(4)) multiplexer_1 (
    .in0(aand_1_out_3), .in1(oor_1_out_3), .in2(xxor_1_out_3), .in3(ssomador4_1_s), .out(in_3), .sel(in_4));
  // Probe on ssomador4_1_s
  Hex_Digit_Display hex_digit_display_1 (.value(in_3));  // open: dp
  // Probe on in_3
endmodule

module AAND (
  input  [3:0] A,
  input  [3:0] B,
  output [3:0] out_3
);

  and and_1 (out_3[0], A[0], B[0]);
  and and_2 (out_3[1], A[1], B[1]);
  and and_3 (out_3[2], A[2], B[2]);
  and and_4 (out_3[3], A[3], B[3]);
endmodule

module OOR (
  input  [3:0] A,
  input  [3:0] B,
  output [3:0] out_3
);

  or or_1 (out_3[0], A[0], B[0]);
  or or_2 (out_3[1], A[1], B[1]);
  or or_3 (out_3[2], A[2], B[2]);
  or or_4 (out_3[3], A[3], B[3]);
endmodule

module XXOR (
  input  [3:0] A,
  input  [3:0] B,
  output [3:0] out_3
);

  xor xor_1 (out_3[0], A[0], B[0]);
  xor xor_2 (out_3[1], A[1], B[1]);
  xor xor_3 (out_3[2], A[2], B[2]);
  xor xor_4 (out_3[3], A[3], B[3]);
endmodule

module SSOMADOR (
  input  a,
  input  b,
  input  cin,
  output s,
  output cout
);

  wire and_1_out, and_2_out, and_3_out, and_4_out, and_5_out, and_6_out, and_7_out, not_1_out, not_2_out,
       not_3_out;

  not not_1 (not_1_out, a);
  not not_2 (not_2_out, b);
  not not_3 (not_3_out, cin);
  and and_1 (and_1_out, not_1_out, not_2_out, cin);
  and and_2 (and_2_out, not_1_out, b, not_3_out);
  and and_3 (and_3_out, a, not_2_out, not_3_out);
  and and_4 (and_4_out, a, b, cin);
  and and_5 (and_5_out, b, cin);
  and and_6 (and_6_out, a, cin);
  and and_7 (and_7_out, a, b);
  or or_1 (s, and_1_out, and_2_out, and_3_out, and_4_out);
  or or_2 (cout, and_5_out, and_6_out, and_7_out);
endmodule

module SSOMADOR4 (
  input  [3:0] A,
  input  [3:0] B,
  output [3:0] S,
  output Carry
);

  wire ssomador_1_cout, ssomador_2_cout, ssomador_3_cout;

  SSOMADOR ssomador_1 (.a(A[0]), .b(B[0]), .cin(1'b0), .s(S[0]), .cout(ssomador_1_cout));
  SSOMADOR ssomador_2 (.a(A[1]), .b(B[1]), .cin(ssomador_1_cout), .s(S[1]), .cout(ssomador_2_cout));
  SSOMADOR ssomador_3 (.a(A[2]), .b(B[2]), .cin(ssomador_2_cout), .s(S[2]), .cout(ssomador_3_cout));
  SSOMADOR ssomador_4 (.a(A[3]), .b(B[3]), .cin(ssomador_3_cout), .s(S[3]), .cout(Carry));
endmodule
